// Logisim project Group5_PartA.circ as structural Verilog: 4 circuits, main circuit Reg16bit
module Reg16bit (
  input  [15:0] regInput,
  input  clk,
  input  we,
  output [15:0] regOutput
);

  Register #(.width(16)) register_1 (.D(regInput), .en(we), .clk(clk), .Q(regOutput));  // open: clr
endmodule

module project_ro (
  input  [15:0] A,
  input  [15:0] B,
  input  [2:0] RU_Selector,
  output RU_Result
);

  wire comparator_1_eq, comparator_1_gt, comparator_1_lt, not_1_out, or_1_out, or_2_out;

  Comparator #(.width(16)) comparator_1 (
    .a(A), .b(B), .gt(comparator_1_gt), .eq(comparator_1_eq), .lt(comparator_1_lt));
  or or_1 (or_1_out, comparator_1_gt, comparator_1_eq);
  or or_2 (or_2_out, comparator_1_lt, comparator_1_eq);
  not not_1 (not_1_out, comparator_1_eq);
  Multiplexer #(.select(3)) multiplexer_1 (
    .in0(comparator_1_gt), .in1(comparator_1_eq), .in2(or_1_out), .in3(comparator_1_lt), .in4(or_2_out),
    .in5(not_1_out), .out(RU_Result), .sel(RU_Selector));  // open: in6, in7

  // Notes on the sheet:
  //   >
  //   >=
  //   <
  //   <=
  //   ==
  //   !-
endmodule

module project_ao (
  input  [15:0] A,
  input  [15:0] B,
  input  [3:0] AUselector,
  output [15:0] AU_Result,
  output [15:0] AU_Dout
);

  wire [15:0] adder_1_out, adder_2_out, and_1_out, divider_1_out, divider_1_rem, multiplexer_1_out,
       multiplier_1_out, negator_1_out, negator_2_out, not_1_out, or_1_out, shifter_1_out, shifter_2_out,
       shifter_3_out, shifter_4_out, xor_1_out;

  Adder #(.width(16)) adder_1 (.a(A), .b(A), .out(adder_1_out));  // open: cin, cout
  assign and_1_out = A & A;  // AND_Gate and_1, 16 bits wide
  assign or_1_out = A | A;  // OR_Gate or_1, 16 bits wide
  Divider #(.width(16)) divider_1 (.a(A), .b(A), .out(divider_1_out), .rem(divider_1_rem));  // open: upper
  Multiplier #(.width(16)) multiplier_1 (.a(A), .b(A), .out(multiplier_1_out));  // open: cin, cout
  assign not_1_out = ~A;  // NOT_Gate not_1, 16 bits wide
  assign xor_1_out = A ^ A;  // XOR_Gate xor_1, 16 bits wide
  Multiplexer #(.width(16)) multiplexer_1 (
    .in0(divider_1_out), .in1(divider_1_rem), .out(multiplexer_1_out), .sel(AUselector[0]));
  Adder #(.width(16)) adder_2 (.a(A), .b(not_1_out), .out(adder_2_out), .cin(1'b1));  // open: cout
  Shifter #(.width(16)) shifter_1 (.in(A), .\dist (4'b0010), .out(shifter_1_out));
  Shifter #(.width(16)) shifter_2 (.in(A), .\dist (4'b0010), .out(shifter_2_out));
  Negator #(.width(16)) negator_1 (.in(A), .out(negator_1_out));
  Negator #(.width(16)) negator_2 (.in(A), .out(negator_2_out));
  Shifter #(.width(16)) shifter_3 (.in(A), .\dist (4'b0010), .out(shifter_3_out));
  Shifter #(.width(16)) shifter_4 (.in(A), .\dist (4'b0010), .out(shifter_4_out));
  Multiplexer #(.select(4), .width(16)) multiplexer_2 (
    .in0(adder_1_out), .in1(and_1_out), .in2(or_1_out), .in3(xor_1_out), .in4(multiplexer_1_out),
    .in5(multiplexer_1_out), .in6(multiplier_1_out), .in7(adder_2_out), .in8(shifter_1_out),
    .in9(shifter_2_out), .in10(shifter_3_out), .in11(shifter_4_out), .in12(negator_1_out),
    .in13(negator_2_out), .out(AU_Dout), .sel(AUselector));  // open: in14, in15

  assign AU_Result = AU_Dout;
  assign B = A;

  // Notes on the sheet:
  //   16-BIT ALU
endmodule

module project_alu (
  input  [15:0] A,
  input  [15:0] B,
  input  [3:0] AU_selector,
  input  [2:0] RU_Selector,
  output [15:0] AU_Result,
  output [15:0] AU_Dout,
  output RU_Result
);

  project_ao project_ao_1 (.A(A), .B(B), .AUselector(AU_selector), .AU_Result(AU_Result), .AU_Dout(AU_Dout));
  project_ro project_ro_1 (.A(A), .B(B), .RU_Selector(RU_Selector), .RU_Result(RU_Result));

  // Notes on the sheet:
  //   16 BITS ALU
endmodule
